# Fritzing sketch HC-SR04 (saved by Fritzing 0.9.4)
breadboards: 1

parts:
  U1 = Arduino Uno (Rev3)
  U2 = HC-SR04 [chip_label=IC package="SIP (Single Inline) [THT]"]

nets:
  N1: U1.D8, U2.Echo
  N2: U1.D9_PWM, U2.Trig
  GND: U1.GND, U2.GND
  5V: U1.5V, U2.Vcc

custom parts:
  HC-SR04: HC-SR04 ultrasound distance sensor
